// Logisim project chapter2.circ as structural Verilog
module HalfAdder (
  input  a,
  input  b,
  output sum,
  output carry
);

  xor xor_1 (sum, b, a);
  and and_1 (carry, b, a);
endmodule

module FullAdder (
  input  c,
  input  b,
  input  a,
  output sum,
  output carry
);

  wire halfadder_1_carry, halfadder_1_sum, not_1_out, or_1_out, xor_1_out;

  HalfAdder halfadder_1 (.a(b), .b(c), .sum(halfadder_1_sum), .carry(halfadder_1_carry));
  xor xor_1 (xor_1_out, b, c);
  or or_1 (or_1_out, c, b);
  not not_1 (not_1_out, xor_1_out);
  Multiplexer #(.enable("false")) multiplexer_1 (.in0(halfadder_1_sum), .in1(not_1_out), .out(sum), .sel(a));
  Multiplexer #(.enable("false")) multiplexer_2 (.in0(halfadder_1_carry), .in1(or_1_out), .out(carry), .sel(a));

  // Notes on the sheet:
  //   xorBC
  //   sumBC
  //   carryBC
  //   orBC
  //   notxorbc
endmodule

module Add16 (
  input  [15:0] a,
  input  [15:0] b,
  output [15:0] out
);

  wire fulladder_1_carry, fulladder_2_carry, fulladder_3_carry, fulladder_4_carry, fulladder_5_carry,
       fulladder_6_carry, fulladder_7_carry, fulladder_8_carry, fulladder_9_carry, fulladder_10_carry,
       fulladder_11_carry, fulladder_12_carry, fulladder_13_carry, fulladder_14_carry, halfadder_1_carry;

  HalfAdder halfadder_1 (.a(a[0]), .b(b[0]), .sum(out[0]), .carry(halfadder_1_carry));
  FullAdder fulladder_1 (.c(halfadder_1_carry), .b(a[1]), .a(b[1]), .sum(out[1]), .carry(fulladder_1_carry));
  FullAdder fulladder_2 (.c(fulladder_1_carry), .b(a[2]), .a(b[2]), .sum(out[2]), .carry(fulladder_2_carry));
  FullAdder fulladder_3 (.c(fulladder_2_carry), .b(a[3]), .a(b[3]), .sum(out[3]), .carry(fulladder_3_carry));
  FullAdder fulladder_4 (.c(fulladder_3_carry), .b(a[4]), .a(b[4]), .sum(out[4]), .carry(fulladder_4_carry));
  FullAdder fulladder_5 (.c(fulladder_4_carry), .b(a[5]), .a(b[5]), .sum(out[5]), .carry(fulladder_5_carry));
  FullAdder fulladder_6 (.c(fulladder_5_carry), .b(a[6]), .a(b[6]), .sum(out[6]), .carry(fulladder_6_carry));
  FullAdder fulladder_7 (.c(fulladder_6_carry), .b(a[7]), .a(b[7]), .sum(out[7]), .carry(fulladder_7_carry));
  FullAdder fulladder_8 (.c(fulladder_7_carry), .b(a[8]), .a(b[8]), .sum(out[8]), .carry(fulladder_8_carry));
  FullAdder fulladder_9 (.c(fulladder_8_carry), .b(a[9]), .a(b[9]), .sum(out[9]), .carry(fulladder_9_carry));
  FullAdder fulladder_10 (.c(fulladder_9_carry), .b(a[10]), .a(b[10]), .sum(out[10]), .carry(fulladder_10_carry));
  FullAdder fulladder_11 (.c(fulladder_10_carry), .b(a[11]), .a(b[11]), .sum(out[11]), .carry(fulladder_11_carry));
  FullAdder fulladder_12 (.c(fulladder_11_carry), .b(a[12]), .a(b[12]), .sum(out[12]), .carry(fulladder_12_carry));
  FullAdder fulladder_13 (.c(fulladder_12_carry), .b(a[13]), .a(b[13]), .sum(out[13]), .carry(fulladder_13_carry));
  FullAdder fulladder_14 (.c(fulladder_13_carry), .b(a[14]), .a(b[14]), .sum(out[14]), .carry(fulladder_14_carry));
  FullAdder fulladder_15 (.c(fulladder_14_carry), .b(a[15]), .a(b[15]), .sum(out[15]));  // open: carry
endmodule

module Inc16 (
  input  [15:0] in,
  output [15:0] out
);

  Add16 add16_1 (.a(in), .b(16'h1), .out(out));
endmodule
